// Logisim project metacpu.circ as structural Verilog: 3 circuits, main circuit main
module main (
  input  [15:0] in_1,
  input  [15:0] in_2,
  input  [3:0] in_3,
  output [15:0] out_4,
  output out_5
);

  ALU alu_1 (.ACC(in_1), .ARB(in_2), .ALUOP(in_3), .Number(out_4), .Overflow(out_5));
endmodule

module ALU (
  input  [15:0] ACC,
  input  [15:0] ARB,
  input  [3:0] ALUOP,
  output [15:0] Number,
  output Overflow
);

  wire adder_1_cout, adder_2_cout, xor_16_out;
  wire [14:0] xor_1_out;

  xor xor_1 (xor_1_out[0], ALUOP[0], ARB[0]);
  xor xor_2 (xor_1_out[2], ARB[2], ALUOP[0]);
  xor xor_3 (xor_1_out[4], ARB[4], ALUOP[0]);
  xor xor_4 (xor_1_out[6], ARB[6], ALUOP[0]);
  xor xor_5 (xor_1_out[8], ARB[8], ALUOP[0]);
  xor xor_6 (xor_1_out[10], ARB[10], ALUOP[0]);
  xor xor_7 (xor_1_out[12], ARB[12], ALUOP[0]);
  xor xor_8 (xor_1_out[14], ARB[14], ALUOP[0]);
  xor xor_9 (xor_1_out[1], ALUOP[0], ARB[1]);
  xor xor_10 (xor_1_out[3], ARB[3], ALUOP[0]);
  xor xor_11 (xor_1_out[5], ARB[5], ALUOP[0]);
  xor xor_12 (xor_1_out[7], ARB[7], ALUOP[0]);
  xor xor_13 (xor_1_out[9], ARB[9], ALUOP[0]);
  xor xor_14 (xor_1_out[11], ARB[11], ALUOP[0]);
  xor xor_15 (xor_1_out[13], ARB[13], ALUOP[0]);
  xor xor_16 (xor_16_out, ARB[15], ALUOP[0]);
  Adder #(.width(15)) adder_1 (.a(ACC[14:0]), .b(xor_1_out), .out(Number[14:0]), .cin(ALUOP[0]), .cout(adder_1_cout));
  Adder #(.width(1)) adder_2 (.a(ACC[15]), .b(xor_16_out), .out(Number[15]), .cin(adder_1_cout), .cout(adder_2_cout));
  xor xor_17 (Overflow, adder_1_cout, adder_2_cout);

  // Notes on the sheet:
  //   ACC is an accumulator
  //   ARB means "Arbitrary value"
  //   Negating an input number by XORing with 1
endmodule

module CONTROL_UNIT (
  input  [7:0] in_1,
  input  [15:0] in_2,
  input  store,
  input  load,
  input  clock,
  input  in_6,
  input  [3:0] ALU_operation,
  input  in_8,
  input  in_9
);

  wire [15:0] alu_1_number, multiplexer_1_out, multiplexer_2_out, ram_1_dout, register_1_q;
  wire [15:8] undriven;

  RAM #(.dataWidth(16)) ram_1 (.addr(in_1), .we(store), .oe(load), .clk(clock), .din(register_1_q), .dout(ram_1_dout));
  Multiplexer #(.enable("false"), .width(16)) multiplexer_1 (
    .in0(alu_1_number), .in1(in_2), .out(multiplexer_1_out), .sel(in_9));
  Register #(.width(16)) register_1 (.D(multiplexer_1_out), .en(in_6), .clk(clock), .Q(register_1_q));  // open: clr
  Multiplexer #(.enable("false"), .width(16)) multiplexer_2 (
    .in0(ram_1_dout), .in1({undriven, in_1}), .out(multiplexer_2_out), .sel(in_8));
  ALU alu_1 (
    .ACC(register_1_q), .ARB(multiplexer_2_out), .ALUOP(ALU_operation), .Number(alu_1_number));  // open: Overflow
  // Pins of 8 and 16 bits meet at {undriven, in_1}

  // Notes on the sheet:
  //   clear acc
  //   enable write to acc
  //   operation mode(memory, imm)
endmodule
